# Fritzing sketch IoT_Course_Project (saved by Fritzing 0.8.7b)
circuit board: 8.46667cm x 5.64444cm
breadboards: 1

parts:
  Raspberry_Pi_1 = Raspberry Pi 4 [part_number=RPI-4-b]
  Adafruit_ADXL345 = Adafruit ADXL345
  DHT11 = DHT11 Humitidy and Temperature Sensor (3 pins)

nets:
  N1: Raspberry_Pi_1.GPIO2, Adafruit_ADXL345.SDA/SDIO
  N2: Raspberry_Pi_1.GPIO3, Adafruit_ADXL345.SCL
  GND: Raspberry_Pi_1.GND, Adafruit_ADXL345.GND, DHT11.GND
  N3: Raspberry_Pi_1.GPIO17, DHT11.DATA
  5V: Raspberry_Pi_1.5V, Adafruit_ADXL345.VIN, DHT11.VDD

custom parts:
  Raspberry Pi 4: The RPi4, a faster version of the awesome Raspberry Pi 2 B ARM Board with 40 pin gpio. Ready for special Raspberry Pi B+ and RPi2 Hat (Hardware attached (on) top)
  Adafruit ADXL345: Filling out our accelerometer offerings, we now have the really lovely digital ADXL345 from Analog Devices, a triple-axis accelerometer with digital I2C and SPI interface breakout. We added an on-board 3.3V regulator and logic-level shifting circuitry, making it a perfect choice for interfacing with any 3V or 5V microcontroller such as the Arduino. The sensor has three axes of measurements, X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
  DHT11 Humitidy and Temperature Sensor (3 pins): DHT11 Humidity and Temperature Sensor (3 pins) from the design created by John De Cristofaro for Adafruit Industries.
